# Fritzing sketch Left_Foot_FSR_PCB (saved by Fritzing 1.0.4)
circuit board: 22.66cm x 30.4756cm
breadboards: 1

parts:
  ESP32L = female pin header, 19 pins [form="♀ (female)"]
  ESP32R = female pin header, 19 pins [form="♀ (female)"]
  mux1L = female pin header, 16 pins [form="♀ (female)"]
  mux2L = female pin header, 16 pins [form="♀ (female)"]
  mux2R = female pin header, 8 pins [form="♀ (female)"]
  mux1R = female pin header, 8 pins [form="♀ (female)"]
  led = female pin header, 2 pins [form="♀ (female)"]
  button = female pin header, 2 pins [form="♀ (female)"]
  batt = female pin header, 2 pins [form="♀ (female)"]
  Rbutton = Resistor [tolerance=±5% power=0.25W resistance=220 package=THT]
  Rled = Resistor [tolerance=±5% power=0.25W resistance=220 package=THT]
  Rmux1 = Resistor [tolerance=±5% power=0.25W resistance=220 package=THT]
  Rmux2 = Resistor [tolerance=±5% power=0.25W resistance=220 package=THT]
  1x1 = female pin header, 2 pins [form="♀ (female)"]
  1x2 = female pin header, 2 pins [form="♀ (female)"]
  1x3 = female pin header, 2 pins [form="♀ (female)"]
  1x4 = female pin header, 2 pins [form="♀ (female)"]
  2x3 = female pin header, 2 pins [form="♀ (female)"]
  2x2 = female pin header, 2 pins [form="♀ (female)"]
  2x1 = female pin header, 2 pins [form="♀ (female)"]
  2x4 = female pin header, 2 pins [form="♀ (female)"]
  3x4 = female pin header, 2 pins [form="♀ (female)"]
  3x3 = female pin header, 2 pins [form="♀ (female)"]
  3x2 = female pin header, 2 pins [form="♀ (female)"]
  3x1 = female pin header, 2 pins [form="♀ (female)"]
  4x4 = female pin header, 2 pins [form="♀ (female)"]
  4x3 = female pin header, 2 pins [form="♀ (female)"]
  4x2 = female pin header, 2 pins [form="♀ (female)"]
  4x1 = female pin header, 2 pins [form="♀ (female)"]
  5x1 = female pin header, 2 pins [form="♀ (female)"]
  5x2 = female pin header, 2 pins [form="♀ (female)"]
  5x3 = female pin header, 2 pins [form="♀ (female)"]
  5x4 = female pin header, 2 pins [form="♀ (female)"]
  6x4 = female pin header, 2 pins [form="♀ (female)"]
  6x3 = female pin header, 2 pins [form="♀ (female)"]
  6x2 = female pin header, 2 pins [form="♀ (female)"]
  6x1 = female pin header, 2 pins [form="♀ (female)"]

nets:
  N1: ESP32L.pin1, batt.pin2
  N2: ESP32L.pin6, ESP32R.pin13, ESP32R.pin19, mux2R.pin1, mux1R.pin1, batt.pin1, Rbutton.Pin_1, Rled.Pin_1, Rmux1.Pin_1, Rmux2.Pin_1
  N3: ESP32L.pin7, mux2R.pin3, mux1R.pin3
  N4: ESP32L.pin8, mux2R.pin4
  N5: ESP32L.pin9, mux2R.pin5
  N6: ESP32L.pin10, mux2R.pin6
  N7: ESP32L.pin11, mux2R.pin7
  N8: ESP32L.pin13, button.pin1, Rbutton.Pin_0
  N9: ESP32L.pin16, mux2R.pin8, Rmux2.Pin_0
  N10: ESP32L.pin17, mux1R.pin8, Rmux1.Pin_0
  N11: ESP32L.pin19, mux2R.pin2, mux1R.pin2, button.pin2, 1x1.pin1, 1x2.pin1, 1x3.pin1, 1x4.pin1, 2x3.pin1, 2x2.pin1, 2x1.pin1, 2x4.pin1, 3x4.pin1, 3x3.pin1, 3x2.pin1, 3x1.pin1, 4x4.pin1, 4x3.pin1, 4x2.pin1, 4x1.pin1, 5x1.pin1, 5x2.pin1, 5x3.pin1, 5x4.pin1, 6x4.pin1, 6x3.pin1, 6x2.pin1, 6x1.pin1
  N12: ESP32R.pin3, led.pin2
  N13: ESP32R.pin4, mux1R.pin7
  N14: ESP32R.pin5, mux1R.pin6
  N15: ESP32R.pin6, mux1R.pin5
  N16: ESP32R.pin7, mux1R.pin4
  N17: mux1L.pin1, 1x1.pin2
  N18: mux1L.pin2, 1x2.pin2
  N19: mux1L.pin3, 1x3.pin2
  N20: mux1L.pin4, 1x4.pin2
  N21: mux1L.pin5, 4x1.pin2
  N22: mux1L.pin6, 3x1.pin2
  N23: mux1L.pin7, 2x1.pin2
  N24: mux1L.pin8, 4x2.pin2
  N25: mux1L.pin9, 3x2.pin2
  N26: mux1L.pin10, 2x2.pin2
  N27: mux1L.pin11, 4x3.pin2
  N28: mux1L.pin12, 3x3.pin2
  N29: mux1L.pin13, 2x3.pin2
  N30: mux1L.pin14, 4x4.pin2
  N31: mux1L.pin15, 3x4.pin2
  N32: mux1L.pin16, 2x4.pin2
  N33: mux2L.pin1, 6x4.pin2
  N34: mux2L.pin2, 5x4.pin2
  N35: mux2L.pin3, 6x3.pin2
  N36: mux2L.pin4, 5x3.pin2
  N37: mux2L.pin5, 6x2.pin2
  N38: mux2L.pin6, 5x2.pin2
  N39: mux2L.pin7, 6x1.pin2
  N40: mux2L.pin8, 5x1.pin2
  N41: led.pin1, Rled.Pin_0

notes:
  USB SIDE
  3V3
  GND
  C0
  Stepio
  January 2025
  5VIN
  Jeanelle Dao
  version 1
  left foot
