# Fritzing sketch Right_Foot_PMW3360_PCB (saved by Fritzing 1.0.4)
circuit board: 4.8cm x 13.8cm
breadboards: 1

parts:
  PMW3360_GND-VDD = double row female pin header, 2 pins [form="♀ (female)"]
  PMW3360_GND-VDDIO = double row female pin header, 2 pins [form="♀ (female)"]
  PWM3360_SPI_Rail = female pin header, 6 pins [form="♀ (female)"]
  ESP32_Left = female pin header, 19 pins [form="♀ (female)"]
  ESP32_Right = female pin header, 19 pins [form="♀ (female)"]
  Rled = Resistor [tolerance=±5% power=0.25W resistance=220 package=THT]
  Button = female pin header, 2 pins [form="♀ (female)"]
  LED = female pin header, 2 pins [form="♀ (female)"]
  FSR = female pin header, 2 pins [form="♀ (female)"]
  Rfsr = Resistor [tolerance=±5% power=0.25W resistance=3300 package=THT]
  batt = female pin header, 2 pins [form="♀ (female)"]
  Dbatt = Diode [package=diode-1n4001]
  Rbutton = Resistor [tolerance=±5% power=0.25W resistance=10000 package=THT]

nets:
  N1: PMW3360_GND-VDD.pin1, PMW3360_GND-VDDIO.pin1, ESP32_Left.pin14, ESP32_Right.pin1, ESP32_Right.pin7, Rled.Pin_1, Rfsr.Pin_1, batt.pin1, Rbutton.Pin_1
  N2: PMW3360_GND-VDD.pin2, PMW3360_GND-VDDIO.pin2, ESP32_Left.pin1, Button.pin2, FSR.pin2
  N3: PWM3360_SPI_Rail.pin1, ESP32_Right.pin13
  N4: PWM3360_SPI_Rail.pin2, ESP32_Right.pin10
  N5: PWM3360_SPI_Rail.pin3, ESP32_Right.pin8
  N6: PWM3360_SPI_Rail.pin4, ESP32_Right.pin2
  N7: PWM3360_SPI_Rail.pin5, ESP32_Right.pin9
  N8: PWM3360_SPI_Rail.pin6, ESP32_Right.pin3
  N9: ESP32_Left.pin3, FSR.pin1, Rfsr.Pin_0
  N10: ESP32_Left.pin7, Button.pin1, Rbutton.Pin_0
  N11: ESP32_Left.pin19, Dbatt.C
  N12: ESP32_Right.pin17, LED.pin2
  N13: Rled.Pin_0, LED.pin1
  N14: batt.pin2, Dbatt.A

notes:
  PMW3360
  GND
  +
  ESP32
  (USB SIDE)
  Stepio
  Jeanelle Dao
  January 2025
  version 1
  right foot
  (    )
